# Fritzing sketch Fritzing 2 (saved by Fritzing 1.0.6)
breadboards: 1

parts:
  VCC1 = Battery [internal_resistance=0.1Ω]
  U1 = SN74LS14N [package="DIP14 [THT]"]
  LED1 = LED - 5mm [color="Red (633nm)" current=0.030A package="5 mm [THT]"]
  R1 = Resistor [tolerance=±5% power=0.25W resistance=220 package=THT]

nets:
  N1: VCC1.-, U1.GND, LED1.cathode
  N2: VCC1.+, U1.1A, U1.VCC
  N3: U1.1Y, U1.2A
  N4: U1.2Y, U1.3A
  N5: U1.3Y, U1.6A
  N6: U1.4Y, R1.Pin_0
  N7: U1.4A, U1.5Y
  N8: U1.5A, U1.6Y
  N9: LED1.anode, R1.Pin_1
