// Logisim project add.circ as structural Verilog: 1 circuit, main circuit main
module main (
  input  Cin,
  input  a,
  input  b
);

  wire and_1_out, and_2_out, or_1_out, xor_1_out, xor_2_out;

  and and_1 (and_1_out, b, a);
  xor xor_1 (xor_1_out, a, b);
  or or_1 (or_1_out, and_1_out, and_2_out);
  and and_2 (and_2_out, xor_1_out, Cin);
  xor xor_2 (xor_2_out, Cin, xor_1_out);
  // Probe on xor_2_out

  // Notes on the sheet:
  //   Cout
  //   s
endmodule
