// Logisim project sub_add_multiplaxer.circ as structural Verilog: 1 circuit, main circuit b1
// sum
module b1 (
  input  Cin,
  input  b0,
  input  a0,
  input  b2,
  input  a1,
  input  b2_2,
  input  b3,
  input  a2,
  input  a3
);

  wire and_1_out, and_2_out, and_3_out, and_4_out, and_5_out, and_6_out, and_7_out, and_8_out,
       multiplexer_1_out, multiplexer_2_out, multiplexer_3_out, multiplexer_4_out, not_1_out, not_2_out,
       not_3_out, not_4_out, or_1_out, or_2_out, or_3_out, or_4_out, xor_1_out, xor_2_out, xor_3_out,
       xor_4_out, xor_5_out, xor_6_out, xor_7_out, xor_8_out;

  not not_1 (not_1_out, b2);
  not not_2 (not_2_out, b2_2);
  not not_3 (not_3_out, b0);
  Multiplexer #(.enable("false")) multiplexer_1 (.in0(b2), .in1(not_1_out), .out(multiplexer_1_out), .sel(Cin));
  Multiplexer #(.enable("false")) multiplexer_2 (.in0(b2_2), .in1(not_2_out), .out(multiplexer_2_out), .sel(Cin));
  Multiplexer #(.enable("false")) multiplexer_3 (.in0(b0), .in1(not_3_out), .out(multiplexer_3_out), .sel(Cin));
  and and_1 (and_1_out, a1, multiplexer_1_out);
  and and_2 (and_2_out, a2, multiplexer_2_out);
  and and_3 (and_3_out, a0, multiplexer_3_out);
  xor xor_1 (xor_1_out, multiplexer_3_out, a0);
  or or_1 (or_1_out, and_3_out, and_4_out);
  xor xor_2 (xor_2_out, multiplexer_1_out, a1);
  or or_2 (or_2_out, and_1_out, and_5_out);
  xor xor_3 (xor_3_out, multiplexer_2_out, a2);
  or or_3 (or_3_out, and_2_out, and_6_out);
  and and_4 (and_4_out, xor_1_out, Cin);
  and and_5 (and_5_out, xor_2_out, or_1_out);
  and and_6 (and_6_out, xor_3_out, or_2_out);
  xor xor_4 (xor_4_out, Cin, xor_1_out);
  // Probe on xor_5_out
  xor xor_5 (xor_5_out, or_1_out, xor_2_out);
  xor xor_6 (xor_6_out, or_2_out, xor_3_out);
  // Probe on xor_6_out
  // Probe on xor_4_out
  not not_4 (not_4_out, b3);
  Multiplexer #(.enable("false")) multiplexer_4 (.in0(b3), .in1(not_4_out), .out(multiplexer_4_out), .sel(Cin));
  and and_7 (and_7_out, a3, multiplexer_4_out);
  xor xor_7 (xor_7_out, multiplexer_4_out, a3);
  or or_4 (or_4_out, and_7_out, and_8_out);
  and and_8 (and_8_out, xor_7_out, or_3_out);
  xor xor_8 (xor_8_out, or_3_out, xor_7_out);
  // Probe on xor_8_out

  // Notes on the sheet:
  //   Cout
  //   Cout
  //   Cout
  //   s1
  //   s2
  //   s0
  //   Cout
  //   s3
endmodule
