// Logisim project sub_add_xor.circ as structural Verilog: 1 circuit, main circuit b1
// sum
module b1 (
  input  Cin,
  input  b0,
  input  a0,
  input  b2,
  input  a1,
  input  b2_2,
  input  b3,
  input  a2,
  input  a3
);

  wire and_1_out, and_2_out, and_3_out, and_4_out, and_5_out, and_6_out, and_7_out, and_8_out, or_1_out,
       or_2_out, or_3_out, or_4_out, xor_1_out, xor_2_out, xor_3_out, xor_4_out, xor_5_out, xor_6_out,
       xor_7_out, xor_8_out, xor_9_out, xor_10_out, xor_11_out, xor_12_out;

  xor xor_1 (xor_1_out, Cin, b0);
  xor xor_2 (xor_2_out, Cin, b2);
  and and_1 (and_1_out, a1, xor_2_out);
  xor xor_3 (xor_3_out, Cin, b2_2);
  and and_2 (and_2_out, a2, xor_3_out);
  and and_3 (and_3_out, a0, xor_1_out);
  xor xor_4 (xor_4_out, xor_1_out, a0);
  or or_1 (or_1_out, and_3_out, and_4_out);
  xor xor_5 (xor_5_out, xor_2_out, a1);
  or or_2 (or_2_out, and_1_out, and_5_out);
  xor xor_6 (xor_6_out, xor_3_out, a2);
  or or_3 (or_3_out, and_2_out, and_6_out);
  and and_4 (and_4_out, xor_4_out, Cin);
  and and_5 (and_5_out, xor_5_out, or_1_out);
  and and_6 (and_6_out, xor_6_out, or_2_out);
  xor xor_7 (xor_7_out, Cin, xor_4_out);
  xor xor_8 (xor_8_out, or_1_out, xor_5_out);
  // Probe on xor_8_out
  xor xor_9 (xor_9_out, or_2_out, xor_6_out);
  // Probe on xor_9_out
  // Probe on xor_7_out
  xor xor_10 (xor_10_out, Cin, b3);
  and and_7 (and_7_out, a3, xor_10_out);
  xor xor_11 (xor_11_out, xor_10_out, a3);
  or or_4 (or_4_out, and_7_out, and_8_out);
  and and_8 (and_8_out, xor_11_out, or_3_out);
  xor xor_12 (xor_12_out, or_3_out, xor_11_out);
  // Probe on xor_12_out

  // Notes on the sheet:
  //   Cout
  //   Cout
  //   Cout
  //   s1
  //   s2
  //   s0
  //   Cout
  //   s3
endmodule
